# Fritzing sketch 회로도 (saved by Fritzing 0.9.3b)
breadboards: 1

parts:
  부품1 = Arduino Uno (Rev3) - ICSP
  LED1 = smd LED [color="Red (633nm)" package="0603 [SMD]"]
  LED2 = smd LED [color="Green (555nm)" package="0603 [SMD]"]
  LED3 = smd LED [color="Blue (430nm)" package="0603 [SMD]"]
  LED4 = smd LED [color="Yellow (585nm)" package="0603 [SMD]"]
  M1 = fc-51 [package=THT]
  M2 = fc-51 [package=THT]
  M3 = fc-51 [package=THT]
  M4 = fc-51 [package=THT]
  J1 = Basic Servo
  부품2 = LCD1602-I2C
  부품3 = LCD1602-I2C
  부품4 = LCD1602-I2C
  부품5 = LCD1602-I2C

nets:
  N1: 부품1.A4/SDA, 부품2.SDA, 부품3.SDA, 부품4.SDA, 부품5.SDA
  N2: 부품1.A5/SCL, 부품2.SCL, 부품3.SCL, 부품4.SCL, 부품5.SCL
  N3: 부품1.D8, LED1.anode
  N4: 부품1.D9_PWM, LED3.anode
  N5: 부품1.D10_PWM/SS, LED2.anode
  N6: 부품1.D11_PWM/MOSI, LED4.anode
  N7: 부품1.D3_PWM, M4.pin1
  N8: 부품1.D4, M3.pin1
  N9: 부품1.D5_PWM, M2.pin1
  N10: 부품1.D6_PWM, M1.pin1
  N11: 부품1.D7, J1.pulse
  5V: 부품1.5V, M1.pin3, M2.pin3, M3.pin3, M4.pin3, J1.vcc
  GND: 부품1.GND, LED1.cathode, LED2.cathode, LED3.cathode, LED4.cathode, M1.pin2, M2.pin2, M3.pin2, M4.pin2, J1.gnd
  GND_2: 부품2.GND, 부품3.GND, 부품4.GND, 부품5.GND
  VCC: 부품2.VCC, 부품3.VCC, 부품4.VCC, 부품5.VCC

custom parts:
  LCD1602-I2C: A standard character display, usually with 2x16 characters. Comes in many colors with LCM1602 IIC attached.
